# Fritzing sketch motor_persiana (saved by Fritzing 0.9.3b)
breadboards: 1

parts:
  Componente1 = Arduino Uno (Rev3)
  S1 = H-Bridge with L298N
  VCC1 = Battery block 9V
  M1 = DC Motor

nets:
  N1: Componente1.D11_PWM/MOSI, S1.ENB
  N2: Componente1.D12/MISO, S1.IN4
  N3: Componente1.D13/SCK, S1.IN3
  GND: Componente1.GND, S1.GND, VCC1.-
  N4: S1.12V, VCC1.+
  N5: S1.M2-01, M1.pin_2
  N6: S1.M2-02, M1.pin_1

custom parts:
  H-Bridge with L298N: h-bridge
