# Fritzing sketch motor_puerta (saved by Fritzing 0.9.3b)
breadboards: 1

parts:
  Componente1 = Arduino Uno (Rev3)
  M1 = DC Motor
  S1 = H-Bridge with L298N
  VCC1 = Battery block 9V

nets:
  GND: Componente1.GND, S1.GND, VCC1.-
  N1: Componente1.D5_PWM, S1.ENB
  N2: Componente1.D6_PWM, S1.IN4
  N3: Componente1.D7, S1.IN3
  N4: M1.pin_1, S1.M2-02
  N5: M1.pin_2, S1.M2-01
  N6: S1.12V, VCC1.+

custom parts:
  H-Bridge with L298N: h-bridge
