# Fritzing sketch pulsador (saved by Fritzing 0.9.3b)
breadboards: 1

parts:
  Componente1 = Arduino Uno (Rev3)
  S1 = Pushbutton [package="[THT]"]
  R1 = Resistor [tolerance=±5% resistance=100 package=THT]

nets:
  N1: Componente1.D12/MISO, S1.Pin_1, S1.Pin_2, R1.Pin_0
  N2: Componente1.GND, R1.Pin_1
  N3: Componente1.5V, S1.Pin_4
